// Logisim project CPU.circ as structural Verilog: 7 circuits, main circuit cpu_main
module system (
  input  in_1
);

  wire ck, cpu_main_1_led_rd, cpu_main_1_led_wr, cs1, cs2, cs_io_1, cs_io_2, cs_io_3, cs_io_4, cs_io_5,
       cs_io_6, n7_segment_display_1_p1, n7_segment_display_3_p1, output_interface_1_out_6,
       output_interface_1_out_7, output_interface_1_out_8, output_interface_1_out_9,
       output_interface_1_out_10, output_interface_1_out_11, output_interface_1_u0, output_interface_1_u7,
       ram_adapter_1_ram_ck, ram_adapter_1_ram_oe, ram_adapter_1_ram_we;
  wire [3:0] cpu_main_1_cmd;
  wire [9:0] ram_adapter_1_ram_addr, rom_adapter_1_rom_add;
  wire [31:0] cpu_main_1_address, cpu_main_1_dout, pc, ram_1_dout, ram_adapter_1_ram_datatowr, rom_1_data,
       rom_adapter_1_data;

  Clock clock_1 (.out(ck));
  ROM #(.addrWidth(10), .dataWidth(32)) rom_1 (.addr(rom_adapter_1_rom_add), .data(rom_1_data));
  RAM #(.addrWidth(10), .asyncread("true"), .dataWidth(32)) ram_1 (
    .addr(ram_adapter_1_ram_addr), .we(ram_adapter_1_ram_we), .oe(ram_adapter_1_ram_oe),
    .clk(ram_adapter_1_ram_ck), .din(ram_adapter_1_ram_datatowr), .dout(ram_1_dout));
  // _7_Segment_Display 7_segment_display_1: pin names not known; wires that end beside it: n7_segment_display_1_p1, n7_segment_display_1_p1
  // BCD_to_7_Segment_decoder bcd_to_7_segment_decoder_1: pin names not known
  // Binary_to_BCD_converter binary_to_bcd_converter_1: pin names not known; wires that end beside it: pc[8:0]
  cpu_main cpu_main_1 (
    .\int (in_1), .CK(ck), .din(rom_adapter_1_data), .led_rd(cpu_main_1_led_rd), .led_wr(cpu_main_1_led_wr),
    .pc_value(pc), .address(cpu_main_1_address), .dout(cpu_main_1_dout), .cmd(cpu_main_1_cmd));  // open: ready
  LED led_1 (.in(cpu_main_1_led_rd));
  LED led_2 (.in(cpu_main_1_led_wr));
  _7_Segment_Display u_7_segment_display_2 ();  // open: g, f, a, b, e, d, c, dp
  // _7_Segment_Display 7_segment_display_3: pin names not known; wires that end beside it: n7_segment_display_3_p1, n7_segment_display_3_p1
  // BCD_to_7_Segment_decoder bcd_to_7_segment_decoder_2: pin names not known
  // BCD_to_7_Segment_decoder bcd_to_7_segment_decoder_3: pin names not known; wires that end beside it: cpu_main_1_address
  rom_adapter rom_adapter_1 (
    .address(cpu_main_1_address), .cmd(cpu_main_1_cmd), .rom_data(rom_1_data), .cs(cs1),
    .rom_add(rom_adapter_1_rom_add), .data(rom_adapter_1_data));
  ram_adapter ram_adapter_1 (
    .address(cpu_main_1_address), .cmd(cpu_main_1_cmd), .cs(cs2), .data_to_write(cpu_main_1_dout),
    .ram_ck({ck, ram_adapter_1_ram_ck}), .ram_datatord(ram_1_dout), .ram_addr(ram_adapter_1_ram_addr),
    .ram_we(ram_adapter_1_ram_we), .ram_oe(ram_adapter_1_ram_oe), .ram_datatowr(ram_adapter_1_ram_datatowr),
    .data_to_read(rom_adapter_1_data));
  // cs_memory cs_mem: pin names not known; wires that end beside it: cpu_main_1_dout, rom_adapter_1_data, cpu_main_1_cmd, cpu_main_1_address, cs1, cs2
  cs_io cs_inout (
    .address(cpu_main_1_address), .cs_peripheral_1(cs_io_1), .out_3(cs_io_2), .out_4(cs_io_3),
    .out_5(cs_io_4), .out_6(cs_io_5), .out_7(cs_io_6));  // open: out_8, out_9, out_10, out_11, out_12, out_13, out_14, out_15, out_16, cs_peripheral_16
  TTY #(.cols(64), .rows(16)) tty_1 ();  // open: data, clk, we, clr
  LedBar ledbar_1 (
    .led0(output_interface_1_u7), .led1(output_interface_1_out_11), .led2(output_interface_1_out_10),
    .led3(output_interface_1_out_9), .led4(output_interface_1_out_8), .led5(output_interface_1_out_7),
    .led6(output_interface_1_out_6), .led7(output_interface_1_u0));
  output_interface output_interface_1 (
    .cmd(cpu_main_1_cmd), .wdata(cpu_main_1_dout), .cs(cs_io_2), .ck(ck), .U0(output_interface_1_u0),
    .out_6(output_interface_1_out_6), .out_7(output_interface_1_out_7), .out_8(output_interface_1_out_8),
    .out_9(output_interface_1_out_9), .out_10(output_interface_1_out_10), .out_11(output_interface_1_out_11),
    .U7(output_interface_1_u7));
  Keyboard keyboard_1 ();  // open: clk, re, clr, avail, data

  // Notes on the sheet:
  //   Program
  //   Counter
  //   Value
  //   contents of rom_1 (hex, n*v repeats v):
  //   28010000 28020005 28210001 70221800 6860fffd 28040001 a8040100
  //   Ram-variables (add:)
  //   rd
  //   wr
  //   Rom-program (add: 0000 0000h)
  //   led_7
  //   led_0
endmodule

module cpu_main (
  input  CK,
  input  \int ,
  input  ready,
  input  [31:0] din,
  output [31:0] pc_value,
  output [31:0] address,
  output [31:0] dout,
  output [3:0] cmd,
  output led_rd,
  output led_wr
);

  wire udc_main_1_cost_enable, udc_main_1_rd1, udc_main_1_rd2, udc_main_1_u, udc_main_1_wr;
  wire [2:0] dp_main_1_flags, udc_main_1_cond;
  wire [4:0] udc_main_1_out_12, udc_main_1_out_14, udc_main_1_out_16;
  wire [31:0] udc_main_1_cost, udc_main_1_reg_ctrl;

  udc_main udc_main_1 (
    .ZF(dp_main_1_flags[0]), .INT(\int ), .ir_in(din), .CK(CK), .ready(ready), .U(udc_main_1_u),
    .cond(udc_main_1_cond), .cost_enable(udc_main_1_cost_enable), .cmd_signals(cmd),
    .reg_ctrl(udc_main_1_reg_ctrl), .RD1(udc_main_1_rd1), .out_12(udc_main_1_out_12), .RD2(udc_main_1_rd2),
    .out_14(udc_main_1_out_14), .WR(udc_main_1_wr), .out_16(udc_main_1_out_16), .COST(udc_main_1_cost));  // open: ask_ready
  or or_1 (led_rd, cmd[0], cmd[2]);
  or or_2 (led_wr, cmd[1], cmd[3]);
  dp_main dp_main_1 (
    .WR(udc_main_1_wr), .c_en(udc_main_1_reg_ctrl[13:11]), .Waddr(udc_main_1_out_16),
    .addrMux(udc_main_1_reg_ctrl[30]), .cost_en(udc_main_1_cost_enable), .RD1(udc_main_1_rd1),
    .Raddr1(udc_main_1_out_12), .a_en(udc_main_1_reg_ctrl[7:5]), .b_en(udc_main_1_reg_ctrl[10:8]),
    .Raddr2(udc_main_1_out_14), .RD2(udc_main_1_rd2), .pc_en(udc_main_1_reg_ctrl[16:14]),
    .temp_en(udc_main_1_reg_ctrl[19:17]), .iar_en(udc_main_1_reg_ctrl[22:20]),
    .mar_en(udc_main_1_reg_ctrl[25:23]), .mdr_en(udc_main_1_reg_ctrl[28:26]), .cost_in(udc_main_1_cost),
    .U(udc_main_1_u), .cond(udc_main_1_cond), .alu_ctrl(udc_main_1_reg_ctrl[4:0]),
    .dataMux(udc_main_1_reg_ctrl[29]), .CK(CK), .data_in(din), .address_out(address), .data_out(dout),
    .pc_state(pc_value), .flags(dp_main_1_flags));
endmodule

module cs_memory (
  input  [31:0] address,
  output cs_mem_1,
  output out_3,
  output out_4,
  output out_5,
  output out_6,
  output out_7,
  output out_8,
  output out_9,
  output out_10,
  output out_11,
  output out_12,
  output out_13,
  output out_14,
  output out_15,
  output out_16,
  output cs_mem_16
);

  Decoder #(.enable("false"), .select(4)) decoder_1 (
    .out0(cs_mem_1), .out1(out_3), .out2(out_4), .out3(out_5), .out4(out_6), .out5(out_7), .out6(out_8),
    .out7(out_9), .out8(out_10), .out9(out_11), .out10(out_12), .out11(out_13), .out12(out_14),
    .out13(out_15), .out14(out_16), .out15(cs_mem_16), .sel(address[13:10]));

  // Notes on the sheet:
  //   i=10
endmodule

module cs_io (
  input  [31:0] address,
  output cs_peripheral_1,
  output out_3,
  output out_4,
  output out_5,
  output out_6,
  output out_7,
  output out_8,
  output out_9,
  output out_10,
  output out_11,
  output out_12,
  output out_13,
  output out_14,
  output out_15,
  output out_16,
  output cs_peripheral_16
);

  Decoder #(.enable("false"), .select(4)) decoder_1 (
    .out0(cs_peripheral_1), .out1(out_3), .out2(out_4), .out3(out_5), .out4(out_6), .out5(out_7),
    .out6(out_8), .out7(out_9), .out8(out_10), .out9(out_11), .out10(out_12), .out11(out_13), .out12(out_14),
    .out13(out_15), .out14(out_16), .out15(cs_peripheral_16), .sel(address[11:8]));

  // Notes on the sheet:
  //   i=8
endmodule

module rom_adapter (
  input  cs,
  input  [3:0] cmd,
  input  [31:0] rom_data,
  input  [31:0] address,
  output [9:0] rom_add,
  output [31:0] data
);

  wire add_en;

  Multiplexer #(.width(10)) multiplexer_1 (.in0({10{1'b0}}), .in1(address[9:0]), .out(rom_add), .sel(add_en));
  and and_1 (add_en, cs, cmd[0]);
  assign data = add_en ? rom_data : 32'bz;  // Controlled_Buffer controlled_buffer_1

  // Notes on the sheet:
  //   memrd
endmodule

module ram_adapter (
  input  cs,
  input  [3:0] cmd,
  input  ck,
  input  [31:0] data_to_write,
  input  [31:0] ram_datatord,
  input  [31:0] address,
  output [9:0] ram_addr,
  output ram_we,
  output ram_oe,
  output ram_ck,
  output [31:0] ram_datatowr,
  output [31:0] data_to_read
);

  wire add_en;

  Multiplexer #(.width(10)) multiplexer_1 (.in0({10{1'b0}}), .in1(address[9:0]), .out(ram_addr), .sel(add_en));
  and and_1 (ram_oe, cs, cmd[0]);
  and and_2 (ram_we, cs, cmd[1]);
  or or_1 (add_en, ram_oe, ram_we);
  assign ram_datatowr = ram_we ? data_to_write : 32'bz;  // Controlled_Buffer controlled_buffer_1
  RAM #(.addrWidth(10), .asyncread("true"), .dataWidth(32)) ram_1 ();  // open: addr, we, oe, clk, din, dout
  assign data_to_read = ram_oe ? ram_datatord : 32'bz;  // Controlled_Buffer controlled_buffer_2

  assign ram_ck = ck;

  // Notes on the sheet:
  //   memrd
endmodule

module output_interface (
  input  cs,
  input  [3:0] cmd,
  input  ck,
  input  [31:0] wdata,
  output U0,
  output out_6,
  output out_7,
  output out_8,
  output out_9,
  output out_10,
  output out_11,
  output U7
);

  wire and_1_out;

  and and_1 (and_1_out, cs, cmd[3]);
  Register register_1 (
    .D(wdata[7:0]), .en(and_1_out), .Q({U7, out_11, out_10, out_9, out_8, out_7, out_6, U0}), .clk(ck));  // open: clr

  // Notes on the sheet:
  //   IO-WR
endmodule
