// Logisim project PIC.circ as structural Verilog: 4 circuits, main circuit pic_main
module pic_main (
  input  CK,
  input  cs,
  input  [3:0] cmd,
  input  [31:0] addr,
  input  [31:0] wdata,
  input  not_INTA,
  input  IR0,
  input  in_8,
  input  in_9,
  input  in_10,
  input  in_11,
  input  in_12,
  input  in_13,
  input  IR7,
  output [31:0] rdata,
  output ready,
  output INT
);

  wire aeoi, and_1_out, and_2_out, and_4_out, and_5_out, and_6_out, and_7_out, and_8_out, ask_aeoi,
       comparator_1_eq, data_mux, decoder_1_out0, decoder_1_out1, decoder_1_out2, IRi, ltim, priority_reset;
  wire [1:0] icw_controller_1_q0;
  wire [2:0] adder_1_out, inta_controller_1_q0, IRR_en, ISR_en, priority_encoder_1_out, register_2_q;
  wire [4:0] addr_msb;
  wire [7:0] and_3_out, eightbit_register_main_1_state, eightbit_register_main_1_u1,
       eightbit_register_main_1_u2, eightbit_register_main_2_state, masked_bits, multiplexer_1_out,
       multiplexer_2_out, not_1_out, priority_resolution_1_u, register_3_q;
  wire [7:1] register_1_q;
  wire [11:8] rom_1_data;

  and and_1 (and_1_out, cs, cmd[2]);
  and and_2 (and_2_out, cs, cmd[3]);
  assign not_1_out = ~masked_bits;  // NOT_Gate not_1, 8 bits wide
  assign and_3_out = not_1_out & {IR7, in_13, in_12, in_11, in_10, in_9, in_8, IR0};  // AND_Gate and_3, 8 bits wide
  icw_controller icw_controller_1 (
    .a0(addr[0]), .wr(and_2_out), .in_3(CK), .q0(icw_controller_1_q0[0]), .q1(icw_controller_1_q0[1]));
  Decoder #(.enable("false"), .select(2)) decoder_1 (
    .out0(decoder_1_out0), .out1(decoder_1_out1), .out2(decoder_1_out2), .out3(ready),
    .sel(icw_controller_1_q0));
  inta_controller inta_controller_1 (
    .not_INTA(not_INTA), .CK(CK), .IRi(IRi), .q2(inta_controller_1_q0[2]), .q0(inta_controller_1_q0[0]),
    .q1(inta_controller_1_q0[1]));
  or or_1 (INT, inta_controller_1_q0[0], inta_controller_1_q0[1], inta_controller_1_q0[2]);
  Multiplexer #(.width(8)) multiplexer_1 (.in0({8{1'b0}}), .in1(and_3_out), .out(multiplexer_1_out), .sel(ready));
  and and_4 (and_4_out, ask_aeoi, aeoi);
  ROM #(.addrWidth(3), .dataWidth(12)) rom_1 (
    .addr(adder_1_out),
    .data({rom_1_data[11], ask_aeoi, rom_1_data[9:8], ISR_en, IRR_en, data_mux, priority_reset}));
  Adder #(.width(3)) adder_1 (.a(inta_controller_1_q0), .b(3'b000), .out(adder_1_out), .cin(and_4_out));  // open: cout
  not not_2 (IRi, comparator_1_eq);
  Comparator #(.mode("unsigned")) comparator_1 (
    .a(multiplexer_1_out), .b({8{1'b0}}), .eq(comparator_1_eq));  // open: gt, lt
  and and_5 (and_5_out, and_2_out, decoder_1_out0);
  and and_6 (and_6_out, and_2_out, decoder_1_out1);
  and and_7 (and_7_out, and_2_out, decoder_1_out2);
  // Probe on eightbit_register_main_1_u1
  // Probe on eightbit_register_main_1_u2
  Register register_1 (.D({{7{1'b0}}, wdata[0]}), .en(and_5_out), .Q({register_1_q, ltim}), .clk(CK));  // open: clr
  Register register_2 (.D({wdata[7:3], 3'b000}), .en(and_6_out), .Q({addr_msb, register_2_q}), .clk(CK));  // open: clr
  Register register_3 (
    .D({{6{1'b0}}, wdata[1:0]}), .en(and_7_out), .Q({register_3_q[7:2], aeoi, register_3_q[0]}), .clk(CK));  // open: clr
  priority_resolution priority_resolution_1 (
    .A(eightbit_register_main_1_u1), .B(eightbit_register_main_1_u2), .reset(priority_reset),
    .U(priority_resolution_1_u));
  eightbit_register_main eightbit_register_main_1 (
    .D(multiplexer_2_out), .CK(CK), .reg_ctrl(IRR_en), .state(eightbit_register_main_1_state),
    .U1(eightbit_register_main_1_u1), .U2(eightbit_register_main_1_u2));
  Multiplexer #(.width(8)) multiplexer_2 (
    .in0(multiplexer_1_out), .in1(priority_resolution_1_u), .out(multiplexer_2_out), .sel(data_mux));
  // Probe on eightbit_register_main_1_state
  eightbit_register_main eightbit_register_main_2 (
    .D(priority_resolution_1_u), .CK(CK), .reg_ctrl(ISR_en), .state(eightbit_register_main_2_state),
    .U1(eightbit_register_main_1_u1), .U2(eightbit_register_main_1_u2));
  // Probe on eightbit_register_main_2_state
  // Probe on priority_resolution_1_u
  Priority_Encoder priority_encoder_1 (
    .in0(eightbit_register_main_1_u2[0]), .in1(eightbit_register_main_1_u2[1]),
    .in2(eightbit_register_main_1_u2[2]), .in3(eightbit_register_main_1_u2[3]),
    .in4(eightbit_register_main_1_u2[4]), .in5(eightbit_register_main_1_u2[5]),
    .in6(eightbit_register_main_1_u2[6]), .in7(eightbit_register_main_1_u2[7]), .out(priority_encoder_1_out));  // open: en_in, gs, en_out
  and and_8 (and_8_out, and_2_out, addr[0], ready);
  assign rdata[7:0] = rom_1_data[11] ? {addr_msb, priority_encoder_1_out} : 8'bz;  // Controlled_Buffer controlled_buffer_1
  Register IMR (.D(wdata[7:0]), .en(and_8_out), .Q(masked_bits), .clk(CK));  // open: clr

  // Notes on the sheet:
  //   iord
  //   iowr
  //   ba[0]
  //   bd[7...0]
  //   bd[7...0]
  //   contents of rom_1 (hex, n*v repeats v):
  //   4 0 a8 0 c80
  //   n
endmodule

module icw_controller (
  input  a0,
  input  wr,
  input  in_3,
  output q0,
  output q1
);

  wire and_1_out, and_2_out, and_3_out, and_4_out, and_5_out, not_1_out, not_2_out, not_3_out, or_1_out,
       or_2_out;

  not not_1 (not_1_out, q1);
  not not_2 (not_2_out, a0);
  and and_1 (and_1_out, not_1_out, not_2_out, wr);
  and and_2 (and_2_out, q1, a0, wr);
  and and_3 (and_3_out, q0, not_3_out);
  not not_3 (not_3_out, wr);
  and and_4 (and_4_out, q1, q0);
  and and_5 (and_5_out, q0, a0, wr);
  or or_1 (or_1_out, and_5_out, q1);
  or or_2 (or_2_out, and_1_out, and_2_out, and_3_out, and_4_out);
  D_Flip_Flop d_ff_1 (.clk(in_3), .D(or_2_out), .Q(q0));  // open: Qn, preset, reset
  D_Flip_Flop d_ff_2 (.clk(in_3), .D(or_1_out), .Q(q1));  // open: Qn, preset, reset

  // Notes on the sheet:
  //   i1
  //   i0
  //   q1
  //   q0
  //   Q0
  //   Q1
endmodule

module inta_controller (
  input  IRi,
  input  not_INTA,
  input  CK,
  output q0,
  output q1,
  output q2
);

  wire and_1_out, and_2_out, and_3_out, and_4_out, and_5_out, and_6_out, and_7_out, not_1_out, not_2_out,
       not_3_out, not_4_out, not_5_out, not_6_out, not_7_out, or_1_out, or_2_out;

  not not_1 (not_1_out, q2);
  not not_2 (not_2_out, q1);
  and and_1 (and_1_out, not_1_out, not_2_out, not_3_out, IRi);
  not not_3 (not_3_out, q0);
  and and_2 (and_2_out, q0, not_INTA);
  and and_3 (and_3_out, q1, not_INTA);
  not not_4 (not_4_out, q1);
  and and_4 (and_4_out, not_4_out, q0, not_5_out);
  not not_5 (not_5_out, not_INTA);
  and and_5 (and_5_out, q1, not_INTA);
  and and_6 (and_6_out, q1, not_6_out);
  not not_6 (not_6_out, q0);
  and and_7 (and_7_out, q1, q0, not_7_out);
  not not_7 (not_7_out, not_INTA);
  or or_1 (or_1_out, and_1_out, and_2_out, and_3_out);
  or or_2 (or_2_out, and_4_out, and_5_out, and_6_out);
  D_Flip_Flop d_ff_1 (.clk(CK), .D(or_1_out), .Q(q0));  // open: Qn, preset, reset
  D_Flip_Flop d_ff_2 (.clk(CK), .D(or_2_out), .Q(q1));  // open: Qn, preset, reset
  D_Flip_Flop d_ff_3 (.clk(CK), .D(and_7_out), .Q(q2));  // open: Qn, preset, reset

  // Notes on the sheet:
  //   I0
  //   I1
  //   q2
  //   q1
  //   q0
  //   Q0
  //   Q1
  //   Q2
endmodule

module priority_resolution (
  input  reset,
  input  [7:0] A,
  input  [7:0] B,
  output [7:0] U
);

  wire not_1_out, priority_encoder_1_en_out;
  wire [2:0] priority_encoder_1_out;
  wire [7:0] and_1_out, decoder_1_out0, not_2_out, or_1_out;

  not not_1 (not_1_out, priority_encoder_1_en_out);
  Priority_Encoder priority_encoder_1 (
    .in0(A[0]), .in1(A[1]), .in2(A[2]), .in3(A[3]), .in4(A[4]), .in5(A[5]), .in6(A[6]), .in7(A[7]),
    .out(priority_encoder_1_out), .en_out(priority_encoder_1_en_out));  // open: en_in, gs
  Decoder #(.select(3)) decoder_1 (
    .out0(decoder_1_out0[0]), .out1(decoder_1_out0[1]), .out2(decoder_1_out0[2]), .out3(decoder_1_out0[3]),
    .out4(decoder_1_out0[4]), .out5(decoder_1_out0[5]), .out6(decoder_1_out0[6]), .out7(decoder_1_out0[7]),
    .sel(priority_encoder_1_out), .en(not_1_out));
  assign or_1_out = decoder_1_out0 | B;  // OR_Gate or_1, 8 bits wide
  assign not_2_out = ~decoder_1_out0;  // NOT_Gate not_2, 8 bits wide
  assign and_1_out = not_2_out & B;  // AND_Gate and_1, 8 bits wide
  Multiplexer #(.width(8)) multiplexer_1 (.in0(or_1_out), .in1(and_1_out), .out(U), .sel(reset));
endmodule
