// Logisim project DataPath.circ as structural Verilog: 1 circuit, main circuit dp_main
module dp_main (
);

  wire [31:0] alu_main_1_u, register_main_1_state, undriven, undriven_2;

  // Probe on nothing
  // Probe on nothing
  // Probe on nothing
  // Probe on nothing
  // Probe on nothing
  // Probe on nothing
  // Probe on nothing
  // Probe on nothing
  // Probe on nothing
  // Probe on nothing
  // Probe on nothing
  // Probe on nothing
  // Probe on nothing
  // Probe on nothing
  // Probe on nothing
  // Probe on nothing
  register_main register_main_1 (.state(register_main_1_state));  // open: D, CK, reg_ctrl, U1, U2
  // Probe on register_main_1_state
  alu_main alu_main_1 (.A(undriven), .B(undriven_2), .U(alu_main_1_u));  // open: alu_ctrl, M, CI, out_flags
  // Probe on nothing
  // Probe on nothing
  // Probe on nothing
  // Probe on nothing
  // Probe on nothing
  // Probe on nothing
  // Probe on nothing
  // Probe on nothing
  // Probe on nothing
  // Probe on nothing
  // Probe on nothing
  // Probe on nothing
  // Probe on nothing
  // Probe on nothing
  // Probe on nothing
  // Probe on nothing
endmodule
